// Logisim project mycirc.circ as structural Verilog: 1 circuit, main circuit aXORb
module aXORb (
  input  A,
  input  B,
  output A_XOR_B
);

  wire and_1_out, and_2_out, notA_out, notB_out;

  not notA (notA_out, A);
  not notB (notB_out, B);
  and and_1 (and_1_out, notA_out, B);
  and and_2 (and_2_out, notB_out, A);
  or or_1 (A_XOR_B, and_1_out, and_2_out);
endmodule
